# Fritzing sketch RFID Attendance Device (saved by Fritzing 0.9.3b)

parts:
  WeMos_D1_Mini1 = WeMos D1 Mini
  RDM1 = RDM6300
  J1 = Piezo Speaker
  S1 = Pushbutton [package=THT]
  LED1 = smd LED [color="Red (633nm)" package="1206 [SMD]"]  # not connected
  R1 = Resistor [tolerance=±5% resistance=10k package="0805 [SMD]"]
  Q1 = MOSFET-NCHANNEL [package=to220v]
  R2 = Resistor [tolerance=±5% resistance=220 package="0805 [SMD]"]
  R3 = Resistor [tolerance=±5% resistance=10k package="0805 [SMD]"]

nets:
  N1: WeMos_D1_Mini1.3V3, S1.leg0
  5V: WeMos_D1_Mini1.5V, RDM1.5V, J1.pin2
  N2: WeMos_D1_Mini1.D4, R2.Pin_0
  N3: WeMos_D1_Mini1.D5, RDM1.Tx
  N4: WeMos_D1_Mini1.D6, Q1.G, R3.Pin_0
  N5: WeMos_D1_Mini1.D8, S1.leg1
  N6: WeMos_D1_Mini1.G, RDM1.GND, R1.Pin_1, Q1.S, R3.Pin_1
  N7: J1.pin1, Q1.D
